// Digital circuit 4bit-comparator.dig as structural Verilog
module _4bit_comparator (
  input  a0,
  input  a1,
  input  a2,
  input  a3,
  input  b0,
  input  b1,
  input  b2,
  input  b3,
  output E
);

  wire xnor_1_out, xnor_2_out, xnor_3_out, xnor_4_out;

  xnor xnor_1 (xnor_1_out, a0, b0);
  xnor xnor_2 (xnor_2_out, a1, b1);
  xnor xnor_3 (xnor_3_out, a2, b2);
  xnor xnor_4 (xnor_4_out, a3, b3);
  and and_1 (E, xnor_1_out, xnor_2_out, xnor_3_out, xnor_4_out);
endmodule
