// Digital circuit 4bit-register.dig as structural Verilog
module _4bit_register (
  input  C,
  input  L,
  input  d0,
  input  d1,
  input  d2,
  input  d3,
  input  R,
  output q0,
  output q1,
  output q2,
  output q3
);

  wire and_1_out, and_2_out, and_3_out, and_4_out, multiplexer_1_out, multiplexer_2_out, multiplexer_3_out,
       multiplexer_4_out, not_1_out;

  Multiplexer multiplexer_1 (.sel(L), .in_0(q0), .in_1(d0), .out(multiplexer_1_out));
  Multiplexer multiplexer_2 (.sel(L), .in_0(q1), .in_1(d1), .out(multiplexer_2_out));
  Multiplexer multiplexer_3 (.sel(L), .in_0(q2), .in_1(d2), .out(multiplexer_3_out));
  Multiplexer multiplexer_4 (.sel(L), .in_0(q3), .in_1(d3), .out(multiplexer_4_out));
  not not_1 (not_1_out, R);
  and and_1 (and_1_out, multiplexer_1_out, not_1_out);
  and and_2 (and_2_out, multiplexer_2_out, not_1_out);
  and and_3 (and_3_out, multiplexer_3_out, not_1_out);
  and and_4 (and_4_out, multiplexer_4_out, not_1_out);
  D_FF d_ff_1 (.D(and_1_out), .C(C), .Q(q0));  // open: nQ
  D_FF d_ff_2 (.D(and_2_out), .C(C), .Q(q1));  // open: nQ
  D_FF d_ff_3 (.D(and_3_out), .C(C), .Q(q2));  // open: nQ
  D_FF d_ff_4 (.D(and_4_out), .C(C), .Q(q3));  // open: nQ
endmodule
