// Digital circuit block.dig as structural Verilog
module block (
  input  C,
  input  A,
  input  R,
  output B
);

  wire and_1_out, rs_ff_1_q, rs_ff_2_q;

  RS_FF rs_ff_1 (.S(A), .C(C), .R(R), .Q(rs_ff_1_q));  // open: nQ
  and and_1 (and_1_out, rs_ff_1_q, A);
  RS_FF rs_ff_2 (.S(and_1_out), .C(C), .R(R), .Q(rs_ff_2_q));  // open: nQ
  or or_1 (B, and_1_out, rs_ff_2_q);
endmodule
