// Digital circuit lock.dig as structural Verilog
module lock (
  input  in_1,
  input  in_2,
  input  in_3,
  input  in_4,
  input  in_5,
  input  in_6,
  input  in_7,
  input  in_8,
  input  Prog,
  input  in_10,
  input  in_11,
  input  in_12,
  input  in_13,
  input  in_14,
  input  in_15,
  input  in_16,
  input  in_17,
  input  Reset,
  input  clock,
  output out_18
);

  wire _4bit_comparator_1_e, _4bit_comparator_2_e, _4bit_comparator_3_e, _4bit_comparator_4_e,
       _4bit_register_1_q0, _4bit_register_1_q1, _4bit_register_1_q2, _4bit_register_1_q3,
       _4bit_register_2_q0, _4bit_register_2_q1, _4bit_register_2_q2, _4bit_register_2_q3,
       _4bit_register_3_q0, _4bit_register_3_q1, _4bit_register_3_q2, _4bit_register_3_q3,
       _4bit_register_4_q0, _4bit_register_4_q1, _4bit_register_4_q2, _4bit_register_4_q3,
       _4bit_register_5_q0, _4bit_register_5_q1, _4bit_register_5_q2, _4bit_register_5_q3,
       _4bit_register_6_q0, _4bit_register_6_q1, _4bit_register_6_q2, _4bit_register_6_q3, and_1_out,
       and_2_out, nor_1_out, not_1_out, not_2_out, state_machine_1_s0, state_machine_1_s1;

  _4bit_register _4bit_register_1 (
    .C(clock), .L(Prog), .d0(in_1), .d1(in_2), .d2(in_3), .d3(in_4), .R(Reset), .q0(_4bit_register_1_q0),
    .q1(_4bit_register_1_q1), .q2(_4bit_register_1_q2), .q3(_4bit_register_1_q3));
  _4bit_register _4bit_register_2 (
    .C(clock), .L(Prog), .d0(in_5), .d1(in_6), .d2(in_7), .d3(in_8), .R(Reset), .q0(_4bit_register_2_q0),
    .q1(_4bit_register_2_q1), .q2(_4bit_register_2_q2), .q3(_4bit_register_2_q3));
  _4bit_register _4bit_register_3 (
    .C(clock), .L(1'b1), .d0(in_10), .d1(in_11), .d2(in_12), .d3(in_13), .R(Reset), .q0(_4bit_register_3_q0),
    .q1(_4bit_register_3_q1), .q2(_4bit_register_3_q2), .q3(_4bit_register_3_q3));
  _4bit_register _4bit_register_4 (
    .C(clock), .L(1'b1), .d0(in_14), .d1(in_15), .d2(in_16), .d3(in_17), .R(Reset), .q0(_4bit_register_4_q0),
    .q1(_4bit_register_4_q1), .q2(_4bit_register_4_q2), .q3(_4bit_register_4_q3));
  _4bit_comparator _4bit_comparator_1 (
    .a0(_4bit_register_2_q0), .a1(_4bit_register_2_q1), .a2(_4bit_register_2_q2), .a3(_4bit_register_2_q3),
    .b0(_4bit_register_4_q0), .b1(_4bit_register_4_q1), .b2(_4bit_register_4_q2), .b3(_4bit_register_4_q3),
    .E(_4bit_comparator_1_e));
  _4bit_comparator _4bit_comparator_2 (
    .a0(_4bit_register_1_q0), .a1(_4bit_register_1_q1), .a2(_4bit_register_1_q2), .a3(_4bit_register_1_q3),
    .b0(_4bit_register_3_q0), .b1(_4bit_register_3_q1), .b2(_4bit_register_3_q2), .b3(_4bit_register_3_q3),
    .E(_4bit_comparator_2_e));
  _4bit_register _4bit_register_5 (
    .C(clock), .L(Prog), .d0(_4bit_register_4_q0), .d1(_4bit_register_4_q1), .d2(_4bit_register_4_q2),
    .d3(_4bit_register_4_q3), .R(Reset), .q0(_4bit_register_5_q0), .q1(_4bit_register_5_q1),
    .q2(_4bit_register_5_q2), .q3(_4bit_register_5_q3));
  _4bit_comparator _4bit_comparator_3 (
    .a0(_4bit_register_4_q0), .a1(_4bit_register_4_q1), .a2(_4bit_register_4_q2), .a3(_4bit_register_4_q3),
    .b0(_4bit_register_5_q0), .b1(_4bit_register_5_q1), .b2(_4bit_register_5_q2), .b3(_4bit_register_5_q3),
    .E(_4bit_comparator_3_e));
  _4bit_register _4bit_register_6 (
    .C(clock), .L(Prog), .d0(_4bit_register_3_q0), .d1(_4bit_register_3_q1), .d2(_4bit_register_3_q2),
    .d3(_4bit_register_3_q3), .R(Reset), .q0(_4bit_register_6_q0), .q1(_4bit_register_6_q1),
    .q2(_4bit_register_6_q2), .q3(_4bit_register_6_q3));
  and and_1 (and_1_out, _4bit_comparator_2_e, _4bit_comparator_1_e);
  and and_2 (and_2_out, _4bit_comparator_4_e, _4bit_comparator_3_e);
  nor nor_1 (nor_1_out, and_2_out, Prog);
  _4bit_comparator _4bit_comparator_4 (
    .a0(_4bit_register_3_q0), .a1(_4bit_register_3_q1), .a2(_4bit_register_3_q2), .a3(_4bit_register_3_q3),
    .b0(_4bit_register_6_q0), .b1(_4bit_register_6_q1), .b2(_4bit_register_6_q2), .b3(_4bit_register_6_q3),
    .E(_4bit_comparator_4_e));
  not not_1 (not_1_out, and_1_out);
  state_machine state_machine_1 (
    .e(not_1_out), .reset(Reset), .clock(clock), .Enable(nor_1_out), .s1(state_machine_1_s1),
    .s0(state_machine_1_s0));
  not not_2 (not_2_out, state_machine_1_s0);
  TransGate transgate_1 (.A(not_2_out), .nA(state_machine_1_s0), .out1(state_machine_1_s1), .out2(out_18));
endmodule
