// Digital circuit state-machine.dig as structural Verilog
module state_machine (
  input  e,
  input  reset,
  input  clock,
  input  Enable,
  output s1,
  output s0
);

  wire and_1_out, and_2_out, and_3_out, and_4_out, multiplexer_1_out, multiplexer_2_out, not_1_out,
       not_2_out, or_1_out, or_2_out, y0_nq, y0_q, y1_nq, y1_q;

  not not_1 (not_1_out, e);
  and and_1 (and_1_out, y1_q, y0_q);
  and and_2 (and_2_out, e, y0_nq);
  or or_1 (or_1_out, y0_q, y1_q, not_1_out);
  or or_2 (or_2_out, and_1_out, and_2_out);
  not not_2 (not_2_out, reset);
  Multiplexer multiplexer_1 (.sel(Enable), .in_0(y1_q), .in_1(or_2_out), .out(multiplexer_1_out));
  Multiplexer multiplexer_2 (.sel(Enable), .in_0(y0_q), .in_1(or_1_out), .out(multiplexer_2_out));
  and and_3 (and_3_out, multiplexer_1_out, not_2_out);
  and and_4 (and_4_out, multiplexer_2_out, not_2_out);
  D_FF y1 (.D(and_3_out), .C(clock), .Q(y1_q), .nQ(y1_nq));
  D_FF y0 (.D(and_4_out), .C(clock), .Q(y0_q), .nQ(y0_nq));
  and and_5 (s0, y1_q, y0_q);
  and and_6 (s1, y1_nq, y0_q);
endmodule
